# Fritzing sketch muxDiagram (saved by Fritzing 1.0.0rc)
breadboards: 1

parts:
  U1 = 74HC4052 [package=dil16]
  U2 = 7-SEGMENT-DISPLAY [package=7-segment-display]
  R1 = Resistor [tolerance=±5% resistance=22 package="2010 [SMD]"]
  R2 = Resistor [tolerance=±5% resistance=22 package="2010 [SMD]"]
  R3 = Resistor [tolerance=±5% resistance=22 package="2010 [SMD]"]
  R4 = Resistor [tolerance=±5% resistance=22 package="2010 [SMD]"]
  R5 = Resistor [tolerance=±5% resistance=22 package="2010 [SMD]"]
  R6 = Resistor [tolerance=±5% resistance=22 package="2010 [SMD]"]
  R7 = Resistor [tolerance=±5% resistance=22 package="2010 [SMD]"]
  R8 = Resistor [tolerance=±5% resistance=22 package="2010 [SMD]"]
  Part1 = Arduino Uno (Rev3) - ICSP
  S1 = Momentary Switch [package=ksa_sealed_tac_switch]
  R9 = Trimmer Potentiometer [maximum_resistance=10kΩ knob_status=50% power=0.5W package=THT]

nets:
  N1: U1.Y0, R3.Pin_0
  N2: U1.Y2, R4.Pin_0
  VCC: U1.Y, U1.VCC, Part1.5V, R9.leg2
  N3: U1.Y3, R1.Pin_1
  N4: U1.Y1, R2.Pin_1
  GND: U1.INH, U1.VEE, U1.GND, U2.C, U2.F, Part1.GND, S1.3, R9.leg1
  N5: U1.B, Part1.D4
  N6: U1.A, Part1.D3_PWM
  N7: U1.X3, Part1.D2
  N8: U1.X0, R7.Pin_1
  N9: U1.X, R8.Pin_1
  N10: U1.X1, R5.Pin_0
  N11: U1.X2, R6.Pin_0
  N12: U2.E, R6.Pin_1
  N13: U2.D, R3.Pin_1
  N14: U2.G1, R4.Pin_1
  N15: U2.DP, R1.Pin_0
  N16: U2.B, R2.Pin_0
  N17: U2.A, R7.Pin_0
  N18: U2.G2, R8.Pin_0
  N19: U2.G, R5.Pin_1
  N20: Part1.A0, S1.1
  N21: Part1.A1, R9.wiper
